// Logisim project CPU.circ as structural Verilog: 2 circuits, main circuit CPU
module CPU (
  input  in_1,
  input  in_2
);

  wire addSignal, aluSignal, cmpSignal, immSignal, incPC, instReadSignal, jumpSignal, ldSignal, not_1_out,
       not_2_out, or_1_out, pcReadSignal, regWrite, stSignal;
  wire [2:0] dest, multiplexer_3_out, multiplexer_4_out, multiplexer_5_out, op1, op2, src1, src2, st_src;
  wire [8:0] jump_addres;
  wire [9:0] ld_st_addres;
  wire [15:0] alu_result, data, imm_value, instruction, multiplexer_1_out, multiplexer_2_out,
       multiplexer_6_out, n16bit_register_1_q_16, op1_value, op2_value, pc_counter_1_p6, reg1_value,
       reg2_value, register_memory_1_reg1_value, register_memory_1_reg2_value, rom_1_data;

  // pc_counter pc_counter_1: pin names not known; wires that end beside it: jump_addres, jumpSignal, incPC, in_1, in_2, pc_counter_1_p6
  Multiplexer #(.width(16), .enable("false")) multiplexer_1 (
    .in1(pc_counter_1_p6), .out(multiplexer_1_out), .sel(pcReadSignal));  // open: in0
  control_unit control_unit_1 (
    .in_3(op1_value), .in_5(op2_value), .imm_signal(immSignal), .instruction(instruction),
    .jump_address(jump_addres), .st_src(st_src), .destination(dest), .src1(src1), .imm_value(imm_value),
    .src2(src2), .ls_st_address(ld_st_addres), .op1(op1), .op2(op2), .out_17(addSignal), .clear(in_2),
    .clock(in_1), .PCReadSignal(pcReadSignal), .instReadSignal(instReadSignal), .ALUSignal(aluSignal),
    .regWrite(regWrite), .LDSignal(ldSignal), .LDSignal_2(stSignal), .CMPSignal(cmpSignal),
    .JUMPSignal(jumpSignal), .incrementPCSignal(incPC));
  ROM #(.addrWidth(16), .dataWidth(16)) rom_1 (.addr(multiplexer_1_out), .data(rom_1_data));  // open: sel
  RAM #(.addrWidth(10), .dataWidth(16), .bus("separate")) ram_1 (
    .addr(ld_st_addres), .din(reg1_value), .data(data), .str(stSignal), .clk(in_1), .ld(ldSignal));  // open: sel, clr
  _16bit_register instruction_register (
    .enable_bit(instReadSignal), .clock(in_1), .clear(in_2), .I_16(rom_1_data), .Q_16(instruction));
  Multiplexer #(.width(16), .enable("false")) multiplexer_2 (
    .in0(alu_result), .in1(data), .out(multiplexer_2_out), .sel(ldSignal));
  or or_1 (or_1_out, ldSignal, aluSignal);
  Multiplexer #(.width(3), .enable("false")) multiplexer_3 (
    .in0(src1), .in1(op1), .out(multiplexer_3_out), .sel(cmpSignal));
  Multiplexer #(.width(3), .enable("false")) multiplexer_4 (
    .in0(src2), .in1(op2), .out(multiplexer_4_out), .sel(cmpSignal));
  _16bit_register u_16bit_register_1 (
    .enable_bit(or_1_out), .clock(in_1), .clear(in_2), .I_16(multiplexer_2_out), .Q_16(n16bit_register_1_q_16));
  Multiplexer #(.width(3), .enable("false")) multiplexer_5 (
    .in0(st_src), .in1(multiplexer_3_out), .out(multiplexer_5_out), .sel(not_1_out));
  not not_1 (not_1_out, stSignal);
  Multiplexer #(.width(16), .enable("false")) multiplexer_6 (
    .in0(reg2_value), .in1(imm_value), .out(multiplexer_6_out), .sel(immSignal));
  not not_2 (not_2_out, addSignal);
  register_memory register_memory_1 (
    .data(n16bit_register_1_q_16), .clear(in_2), .clock(in_1), .read_reg1(multiplexer_5_out),
    .read_reg2(multiplexer_4_out), .reg1_value(register_memory_1_reg1_value),
    .reg2_value(register_memory_1_reg2_value), .write_enable(regWrite), .write_select_reg(dest));
  Demultiplexer #(.width(16), .enable("false")) demultiplexer_1 (
    .out0(reg1_value), .out1(op1_value), .in(register_memory_1_reg1_value), .sel(cmpSignal));
  Demultiplexer #(.width(16), .enable("false")) demultiplexer_2 (
    .out0(reg2_value), .out1(op2_value), .in(register_memory_1_reg2_value), .sel(cmpSignal));
  alu alu_1 (
    .A(reg1_value), .B(multiplexer_6_out), .\output (alu_result), .select_bit(not_2_out),
    .aluSignal(aluSignal));

  // Other names for the same wires on the sheet: clear = in_2; clock = in_1

  // Notes on the sheet:
  //   intruction memory
  //   data memory
  //   contents of rom_1 (hex, n*v repeats v):
  //   2c8c ac02 6885 a802 14a0 b405 d002 3605 ed00 8051 8032 6c99 ac0f 3d05 f70 c801 2885 2ca3 3085 b980
  //   bc04 750 9f80
endmodule

module Project (
);

  wire button_1_out, clock_1_out;

  Button button_1 (.out(button_1_out));
  Clock clock_1 (.out(clock_1_out));
  CPU cpu_1 (.in_2(clock_1_out), .in_1(button_1_out));
endmodule
