// Logisim project alu.circ as structural Verilog: 4 circuits, main circuit half_adder
// HA
module half_adder (
  input  A,
  input  B,
  output \output ,
  output c_out
);

  xor xor_1 (\output , A, B);
  and and_1 (c_out, A, B);
endmodule

// FA
module full_adder (
  input  A,
  input  B,
  input  c_in,
  output \output ,
  output c_out
);

  wire and_1_out, and_2_out, and_3_out;

  xor xor_1 (\output , A, B, c_in);
  and and_1 (and_1_out, A, B);
  and and_2 (and_2_out, B, c_in);
  and and_3 (and_3_out, A, c_in);
  or or_1 (c_out, and_1_out, and_2_out, and_3_out);
endmodule

module adder (
  input  [15:0] A,
  input  [15:0] B,
  output c_out,
  output [15:0] out_4
);

  wire full_adder_2_c_out, full_adder_3_c_out, full_adder_4_c_out, full_adder_5_c_out, full_adder_6_c_out,
       full_adder_7_c_out, full_adder_8_c_out, full_adder_9_c_out, full_adder_10_c_out, full_adder_11_c_out,
       full_adder_12_c_out, full_adder_13_c_out, full_adder_14_c_out, full_adder_15_c_out, half_adder_1_c_out;

  full_adder full_adder_1 (.A(A[15]), .B(B[15]), .c_in(full_adder_2_c_out), .\output (out_4[15]), .c_out(c_out));
  full_adder full_adder_2 (
    .A(A[14]), .B(B[14]), .c_in(full_adder_3_c_out), .\output (out_4[14]), .c_out(full_adder_2_c_out));
  full_adder full_adder_3 (
    .A(A[13]), .B(B[13]), .c_in(full_adder_4_c_out), .\output (out_4[13]), .c_out(full_adder_3_c_out));
  full_adder full_adder_4 (
    .A(A[12]), .B(B[12]), .c_in(full_adder_5_c_out), .\output (out_4[12]), .c_out(full_adder_4_c_out));
  full_adder full_adder_5 (
    .A(A[11]), .B(B[11]), .c_in(full_adder_6_c_out), .\output (out_4[11]), .c_out(full_adder_5_c_out));
  full_adder full_adder_6 (
    .A(A[10]), .B(B[10]), .c_in(full_adder_7_c_out), .\output (out_4[10]), .c_out(full_adder_6_c_out));
  full_adder full_adder_7 (
    .A(A[9]), .B(B[9]), .c_in(full_adder_8_c_out), .\output (out_4[9]), .c_out(full_adder_7_c_out));
  full_adder full_adder_8 (
    .A(A[8]), .B(B[8]), .c_in(full_adder_9_c_out), .\output (out_4[8]), .c_out(full_adder_8_c_out));
  full_adder full_adder_9 (
    .A(A[7]), .B(B[7]), .c_in(full_adder_10_c_out), .\output (out_4[7]), .c_out(full_adder_9_c_out));
  full_adder full_adder_10 (
    .A(A[6]), .B(B[6]), .c_in(full_adder_11_c_out), .\output (out_4[6]), .c_out(full_adder_10_c_out));
  full_adder full_adder_11 (
    .A(A[5]), .B(B[5]), .c_in(full_adder_12_c_out), .\output (out_4[5]), .c_out(full_adder_11_c_out));
  full_adder full_adder_12 (
    .A(A[4]), .B(B[4]), .c_in(full_adder_13_c_out), .\output (out_4[4]), .c_out(full_adder_12_c_out));
  full_adder full_adder_13 (
    .A(A[3]), .B(B[3]), .c_in(full_adder_14_c_out), .\output (out_4[3]), .c_out(full_adder_13_c_out));
  full_adder full_adder_14 (
    .A(A[2]), .B(B[2]), .c_in(full_adder_15_c_out), .\output (out_4[2]), .c_out(full_adder_14_c_out));
  full_adder full_adder_15 (
    .A(A[1]), .B(B[1]), .c_in(half_adder_1_c_out), .\output (out_4[1]), .c_out(full_adder_15_c_out));
  half_adder half_adder_1 (.A(A[0]), .B(B[0]), .\output (out_4[0]), .c_out(half_adder_1_c_out));
endmodule

module alu (
  input  [15:0] A,
  input  [15:0] B,
  input  aluSignal,
  input  select_bit,
  output [15:0] \output 
);

  wire [15:0] adder_1_out_4, and_1_out, multiplexer_1_out;

  adder adder_1 (.A(A), .B(B), .out_4(adder_1_out_4));  // open: c_out
  assign and_1_out = A & B;  // AND_Gate and_1, 16 bits wide
  Multiplexer #(.width(16)) multiplexer_1 (
    .in0(adder_1_out_4), .in1(and_1_out), .out(multiplexer_1_out), .sel(select_bit));  // open: en
  Multiplexer #(.width(16), .enable("false")) multiplexer_2 (
    .in1(multiplexer_1_out), .out(\output ), .sel(aluSignal));  // open: in0
endmodule
