// Logisim project comparator.circ as structural Verilog: 3 circuits, main circuit half_comparator
module half_comparator (
  input  A,
  input  B,
  output gt,
  output lt,
  output eq
);

  wire not_1_out, not_2_out;

  not not_1 (not_1_out, A);
  not not_2 (not_2_out, B);
  and and_1 (gt, not_1_out, B);
  and and_2 (lt, not_2_out, A);
  xnor xnor_1 (eq, B, A);
endmodule

module full_comparator (
  input  A,
  input  B,
  input  gt_in,
  input  lt_in,
  input  eq_in,
  output gt_out,
  output lt_out,
  output eq_out
);

  wire and_1_out, and_2_out, not_1_out, not_2_out, xnor_1_out;

  not not_1 (not_1_out, B);
  not not_2 (not_2_out, A);
  and and_1 (and_1_out, A, eq_in, not_1_out);
  and and_2 (and_2_out, B, eq_in, not_2_out);
  xnor xnor_1 (xnor_1_out, A, B);
  or or_1 (gt_out, and_1_out, gt_in);
  or or_2 (lt_out, and_2_out, lt_in);
  and and_3 (eq_out, xnor_1_out, eq_in);
endmodule

module comparator (
  input  [15:0] op1,
  input  [15:0] op2,
  output gt,
  output lt,
  output eq
);

  wire full_comparator_1_eq_out, full_comparator_1_gt_out, full_comparator_1_lt_out,
       full_comparator_2_eq_out, full_comparator_2_gt_out, full_comparator_2_lt_out,
       full_comparator_3_eq_out, full_comparator_3_gt_out, full_comparator_3_lt_out,
       full_comparator_4_eq_out, full_comparator_4_gt_out, full_comparator_4_lt_out,
       full_comparator_5_eq_out, full_comparator_5_gt_out, full_comparator_5_lt_out,
       full_comparator_6_eq_out, full_comparator_6_gt_out, full_comparator_6_lt_out,
       full_comparator_7_eq_out, full_comparator_7_gt_out, full_comparator_7_lt_out,
       full_comparator_8_eq_out, full_comparator_8_gt_out, full_comparator_8_lt_out,
       full_comparator_9_eq_out, full_comparator_9_gt_out, full_comparator_9_lt_out,
       full_comparator_10_eq_out, full_comparator_10_gt_out, full_comparator_10_lt_out,
       full_comparator_11_eq_out, full_comparator_11_gt_out, full_comparator_11_lt_out,
       full_comparator_12_eq_out, full_comparator_12_gt_out, full_comparator_12_lt_out,
       full_comparator_13_eq_out, full_comparator_13_gt_out, full_comparator_13_lt_out,
       full_comparator_15_eq_out, full_comparator_15_gt_out, full_comparator_15_lt_out, half_comparator_1_eq,
       half_comparator_1_gt, half_comparator_1_lt;

  half_comparator half_comparator_1 (
    .A(op1[15]), .B(op2[15]), .gt(half_comparator_1_gt), .lt(half_comparator_1_lt), .eq(half_comparator_1_eq));
  full_comparator full_comparator_1 (
    .A(op1[14]), .B(op2[14]), .gt_in(half_comparator_1_gt), .lt_in(half_comparator_1_lt),
    .eq_in(half_comparator_1_eq), .gt_out(full_comparator_1_gt_out), .lt_out(full_comparator_1_lt_out),
    .eq_out(full_comparator_1_eq_out));
  full_comparator full_comparator_2 (
    .A(op1[13]), .B(op2[13]), .gt_in(full_comparator_1_gt_out), .lt_in(full_comparator_1_lt_out),
    .eq_in(full_comparator_1_eq_out), .gt_out(full_comparator_2_gt_out), .lt_out(full_comparator_2_lt_out),
    .eq_out(full_comparator_2_eq_out));
  full_comparator full_comparator_3 (
    .A(op1[12]), .B(op2[12]), .gt_in(full_comparator_2_gt_out), .lt_in(full_comparator_2_lt_out),
    .eq_in(full_comparator_2_eq_out), .gt_out(full_comparator_3_gt_out), .lt_out(full_comparator_3_lt_out),
    .eq_out(full_comparator_3_eq_out));
  full_comparator full_comparator_4 (
    .A(op1[11]), .B(op2[11]), .gt_in(full_comparator_3_gt_out), .lt_in(full_comparator_3_lt_out),
    .eq_in(full_comparator_3_eq_out), .gt_out(full_comparator_4_gt_out), .lt_out(full_comparator_4_lt_out),
    .eq_out(full_comparator_4_eq_out));
  full_comparator full_comparator_5 (
    .A(op1[10]), .B(op2[10]), .gt_in(full_comparator_4_gt_out), .lt_in(full_comparator_4_lt_out),
    .eq_in(full_comparator_4_eq_out), .gt_out(full_comparator_5_gt_out), .lt_out(full_comparator_5_lt_out),
    .eq_out(full_comparator_5_eq_out));
  full_comparator full_comparator_6 (
    .A(op1[8]), .B(op2[8]), .gt_in(full_comparator_7_gt_out), .lt_in(full_comparator_7_lt_out),
    .eq_in(full_comparator_7_eq_out), .gt_out(full_comparator_6_gt_out), .lt_out(full_comparator_6_lt_out),
    .eq_out(full_comparator_6_eq_out));
  full_comparator full_comparator_7 (
    .A(op1[9]), .B(op2[9]), .gt_in(full_comparator_5_gt_out), .lt_in(full_comparator_5_lt_out),
    .eq_in(full_comparator_5_eq_out), .gt_out(full_comparator_7_gt_out), .lt_out(full_comparator_7_lt_out),
    .eq_out(full_comparator_7_eq_out));
  full_comparator full_comparator_8 (
    .A(op1[7]), .B(op2[7]), .gt_in(full_comparator_6_gt_out), .lt_in(full_comparator_6_lt_out),
    .eq_in(full_comparator_6_eq_out), .gt_out(full_comparator_8_gt_out), .lt_out(full_comparator_8_lt_out),
    .eq_out(full_comparator_8_eq_out));
  full_comparator full_comparator_9 (
    .A(op1[6]), .B(op2[6]), .gt_in(full_comparator_8_gt_out), .lt_in(full_comparator_8_lt_out),
    .eq_in(full_comparator_8_eq_out), .gt_out(full_comparator_9_gt_out), .lt_out(full_comparator_9_lt_out),
    .eq_out(full_comparator_9_eq_out));
  full_comparator full_comparator_10 (
    .A(op1[5]), .B(op2[5]), .gt_in(full_comparator_9_gt_out), .lt_in(full_comparator_9_lt_out),
    .eq_in(full_comparator_9_eq_out), .gt_out(full_comparator_10_gt_out), .lt_out(full_comparator_10_lt_out),
    .eq_out(full_comparator_10_eq_out));
  full_comparator full_comparator_11 (
    .A(op1[4]), .B(op2[4]), .gt_in(full_comparator_10_gt_out), .lt_in(full_comparator_10_lt_out),
    .eq_in(full_comparator_10_eq_out), .gt_out(full_comparator_11_gt_out),
    .lt_out(full_comparator_11_lt_out), .eq_out(full_comparator_11_eq_out));
  full_comparator full_comparator_12 (
    .A(op1[3]), .B(op2[3]), .gt_in(full_comparator_11_gt_out), .lt_in(full_comparator_11_lt_out),
    .eq_in(full_comparator_11_eq_out), .gt_out(full_comparator_12_gt_out),
    .lt_out(full_comparator_12_lt_out), .eq_out(full_comparator_12_eq_out));
  full_comparator full_comparator_13 (
    .A(op1[2]), .B(op2[2]), .gt_in(full_comparator_12_gt_out), .lt_in(full_comparator_12_lt_out),
    .eq_in(full_comparator_12_eq_out), .gt_out(full_comparator_13_gt_out),
    .lt_out(full_comparator_13_lt_out), .eq_out(full_comparator_13_eq_out));
  full_comparator full_comparator_14 (
    .A(op1[0]), .B(op2[0]), .gt_in(full_comparator_15_gt_out), .lt_in(full_comparator_15_lt_out),
    .eq_in(full_comparator_15_eq_out), .gt_out(gt), .lt_out(lt), .eq_out(eq));
  full_comparator full_comparator_15 (
    .A(op1[1]), .B(op2[1]), .gt_in(full_comparator_13_gt_out), .lt_in(full_comparator_13_lt_out),
    .eq_in(full_comparator_13_eq_out), .gt_out(full_comparator_15_gt_out),
    .lt_out(full_comparator_15_lt_out), .eq_out(full_comparator_15_eq_out));
endmodule
