// Logisim project control_unit.circ as structural Verilog: 3 circuits, main circuit control_unit
module control_unit (
  input  [15:0] instruction,
  input  clear,
  input  [15:0] in_3,
  input  clock,
  input  [15:0] in_5,
  output [2:0] st_src,
  output [2:0] src1,
  output [2:0] src2,
  output [2:0] op1,
  output [2:0] op2,
  output [2:0] destination,
  output [9:0] ls_st_address,
  output [8:0] jump_address,
  output [15:0] imm_value,
  output imm_signal,
  output incrementPCSignal,
  output out_17,
  output JUMPSignal,
  output CMPSignal,
  output ALUSignal,
  output LDSignal,
  output LDSignal_2,
  output regWrite,
  output PCReadSignal,
  output instReadSignal
);

  wire ADD, ADDI, ALUSignal_t, AND, and_7_out, and_8_out, and_9_out, and_10_out, and_11_out, and_19_out,
       and_21_out, and_22_out, and_23_out, and_24_out, and_25_out, ANDI, CF, CMP, comparator_eq,
       comparator_lt, decoder_1_out4, decoder_2_out0, decoder_2_out1, decoder_2_out2, decoder_2_out3,
       decoder_2_out4, decoder_2_out5, JA, JAE, JB, JBE, JE, JUMP, jumpSignal_t, LD, not_1_out, not_2_out,
       not_3_out, not_4_out, not_5_out, or_5_out, regWrite_t, ST, ZF;
  wire [1:0] n2bit_register_1_output, or_9_out;

  and and_1 (JUMP, decoder_2_out0, decoder_1_out4);
  or or_1 (out_17, ADD, ADDI);
  Decoder #(.select(3), .enable("false")) decoder_1 (
    .out0(ADD), .out1(ADDI), .out2(AND), .out3(ANDI), .out4(decoder_1_out4), .out5(LD), .out6(ST),
    .out7(CMP), .sel(instruction[15:13]));
  Decoder #(.select(4)) decoder_2 (
    .out0(decoder_2_out0), .out1(decoder_2_out1), .out2(decoder_2_out2), .out3(decoder_2_out3),
    .out4(decoder_2_out4), .out5(decoder_2_out5), .sel(instruction[3:0]), .en(decoder_1_out4));  // open: out6, out7, out8, out9, out10, out11, out12, out13, out14, out15
  and and_2 (JE, decoder_2_out1, decoder_1_out4);
  or or_2 (imm_signal, ADDI, ANDI);
  and and_3 (JA, decoder_2_out2, decoder_1_out4);
  and and_4 (JB, decoder_2_out3, decoder_1_out4);
  comparator comparator (.op1(in_3), .op2(in_5), .lt(comparator_lt), .eq(comparator_eq));  // open: gt
  and and_5 (JBE, decoder_2_out4, decoder_1_out4);
  or or_3 (ALUSignal_t, ADD, ADDI, AND, ANDI);
  and and_6 (JAE, decoder_2_out5, decoder_1_out4);
  _1bit_register u_1bit_register_1 (.enable_write(CMPSignal), .clock(clock), .clear(clear), .D(comparator_lt), .Q(CF));
  _1bit_register u_1bit_register_2 (.enable_write(CMPSignal), .clock(clock), .clear(clear), .D(comparator_eq), .Q(ZF));
  or or_4 (regWrite_t, ADD, ADDI, AND, ANDI, LD);
  not not_1 (not_1_out, CF);
  not not_2 (not_2_out, CF);
  not not_3 (not_3_out, ZF);
  not not_4 (not_4_out, ZF);
  or or_5 (or_5_out, ZF, CF);
  not not_5 (not_5_out, CF);
  and and_7 (and_7_out, JE, not_1_out, ZF);
  and and_8 (and_8_out, JA, not_2_out, not_3_out);
  and and_9 (and_9_out, JB, CF, not_4_out);
  and and_10 (and_10_out, JBE, or_5_out);
  and and_11 (and_11_out, JAE, not_5_out);
  or or_6 (jumpSignal_t, JUMP, and_7_out, and_8_out, and_9_out, and_10_out, and_11_out);
  and and_12 (ALUSignal, ALUSignal_t, and_19_out);
  and and_13 (LDSignal, LD, and_19_out);
  and and_14 (LDSignal_2, ST, and_19_out);
  and and_15 (PCReadSignal, ~n2bit_register_1_output[1], ~n2bit_register_1_output[0]);  // AND_Gate
  and and_16 (CMPSignal, CMP, and_19_out);
  and and_17 (instReadSignal, ~n2bit_register_1_output[1], n2bit_register_1_output[0]);  // AND_Gate
  assign imm_value = {{9{instruction[6]}}, instruction[6:0]};  // Bit_Extender bit_extender_1
  and and_18 (JUMPSignal, jumpSignal_t, and_19_out);
  and and_19 (and_19_out, n2bit_register_1_output[1], ~n2bit_register_1_output[0]);  // AND_Gate
  and and_20 (regWrite, and_21_out, regWrite_t);
  and and_21 (and_21_out, n2bit_register_1_output[1], n2bit_register_1_output[0]);
  _2bit_register u_2bit_register_1 (
    .clock(clock), .clear(clear), .\output (n2bit_register_1_output), .\input (or_9_out));
  and and_22 (and_22_out, and_21_out, ~jumpSignal_t);  // AND_Gate
  and and_23 (and_23_out, n2bit_register_1_output[0], ~n2bit_register_1_output[1]);  // AND_Gate
  or or_7 (incrementPCSignal, JUMPSignal, and_22_out);
  or or_8 (or_9_out[1], and_23_out, and_24_out);
  and and_24 (and_24_out, ~n2bit_register_1_output[0], n2bit_register_1_output[1]);  // AND_Gate
  and and_25 (and_25_out, ~n2bit_register_1_output[1], ~n2bit_register_1_output[0]);  // AND_Gate
  or or_9 (or_9_out[0], and_24_out, and_25_out);

  assign destination = instruction[12:10];
  assign jump_address = instruction[12:4];
  assign ls_st_address = instruction[9:0];
  assign op1 = instruction[12:10];
  assign op2 = instruction[9:7];
  assign src1 = instruction[9:7];
  assign src2 = instruction[6:4];
  assign st_src = instruction[12:10];

  // Other names for the same wires on the sheet: imm7[6:0] = instruction[6:0]; jump_selector[3:0] = instruction[3:0];
  //   ld_st_address[9:0] = instruction[9:0]; opcode[2:0] = instruction[15:13]; dest[2:0] = instruction[12:10];
  //   src_st[2:0] = instruction[12:10]

  // Notes on the sheet:
  //   Signal Handling
  //   Instruction Parser
  //   Finite State Machine
  //   Control Unit Outputs
endmodule

module _2bit_register (
  input  [1:0] \input ,
  input  clock,
  input  clear,
  output [1:0] \output 
);

  flip_flop flip_flop_1 (.D(\input [1]), .Clock(clock), .clear(clear), .Q(\output [1]));
  flip_flop flip_flop_2 (.D(\input [0]), .Clock(clock), .clear(clear), .Q(\output [0]));
endmodule

module _1bit_register (
  input  D,
  input  enable_write,
  input  clock,
  input  clear,
  output Q
);

  wire multiplexer_1_out;

  Multiplexer #(.enable("false")) multiplexer_1 (.in0(Q), .in1(D), .out(multiplexer_1_out), .sel(enable_write));
  flip_flop flip_flop_1 (.D(multiplexer_1_out), .Clock(clock), .clear(clear), .Q(Q));
endmodule
