// Logisim project pc_register.circ as structural Verilog: 1 circuit, main circuit pc_register
module pc_register (
  input  [8:0] offset,
  input  addOffsetSignal,
  input  increment_PC,
  input  clock,
  input  clear,
  output [15:0] PC
);

  wire [15:0] adder_1_out_4, bit_extender_1_out, multiplexer_1_out;

  assign bit_extender_1_out = {{7{offset[8]}}, offset};  // Bit_Extender bit_extender_1
  Multiplexer #(.width(16), .enable("false")) multiplexer_1 (
    .in0(16'h1), .in1(bit_extender_1_out), .out(multiplexer_1_out), .sel(addOffsetSignal));
  adder adder_1 (.A(multiplexer_1_out), .B(PC), .out_4(adder_1_out_4));  // open: c_out
  _16bit_register u_16bit_register_1 (
    .enable_bit(increment_PC), .clock(clock), .clear(clear), .I_16(adder_1_out_4), .Q_16(PC));
endmodule
