// Logisim project register_file.circ as structural Verilog: 4 circuits, main circuit d_latch
// D Latch
module d_latch (
  input  D,
  input  C,
  output Q
);

  wire and_1_out, and_2_out, nor_1_out, not_1_out;

  not not_1 (not_1_out, D);
  and and_1 (and_1_out, D, C);
  and and_2 (and_2_out, C, not_1_out);
  nor nor_1 (nor_1_out, and_1_out, Q);
  nor nor_2 (Q, nor_1_out, and_2_out);
endmodule

// Flip Flop
module flip_flop (
  input  D,
  input  Clock,
  input  clear,
  output Q
);

  wire d_latch_1_q, multiplexer_1_out, not_1_out;

  Multiplexer #(.enable("false")) multiplexer_1 (.in0(D), .in1(1'b0), .out(multiplexer_1_out), .sel(clear));
  d_latch d_latch_1 (.D(multiplexer_1_out), .C(not_1_out), .Q(d_latch_1_q));
  not not_1 (not_1_out, Clock);
  d_latch d_latch_2 (.D(d_latch_1_q), .C(Clock), .Q(Q));
endmodule

// reg(16)
module _16bit_register (
  input  [15:0] I_16,
  input  enable_bit,
  input  clock,
  input  clear,
  output [15:0] Q_16
);

  wire multiplexer_1_out, multiplexer_2_out, multiplexer_3_out, multiplexer_4_out, multiplexer_5_out,
       multiplexer_6_out, multiplexer_7_out, multiplexer_8_out, multiplexer_9_out, multiplexer_10_out,
       multiplexer_11_out, multiplexer_12_out, multiplexer_13_out, multiplexer_14_out, multiplexer_15_out,
       multiplexer_16_out;

  Multiplexer multiplexer_1 (.in0(Q_16[15]), .in1(I_16[15]), .out(multiplexer_1_out), .sel(enable_bit));  // open: en
  Multiplexer multiplexer_2 (.in0(Q_16[14]), .in1(I_16[14]), .out(multiplexer_2_out), .sel(enable_bit));  // open: en
  flip_flop flip_flop_1 (.D(multiplexer_1_out), .Clock(clock), .clear(clear), .Q(Q_16[15]));
  Multiplexer multiplexer_3 (.in0(Q_16[13]), .in1(I_16[13]), .out(multiplexer_3_out), .sel(enable_bit));  // open: en
  flip_flop flip_flop_2 (.D(multiplexer_2_out), .Clock(clock), .clear(clear), .Q(Q_16[14]));
  Multiplexer multiplexer_4 (.in0(Q_16[12]), .in1(I_16[12]), .out(multiplexer_4_out), .sel(enable_bit));  // open: en
  flip_flop flip_flop_3 (.D(multiplexer_3_out), .Clock(clock), .clear(clear), .Q(Q_16[13]));
  Multiplexer multiplexer_5 (.in0(Q_16[11]), .in1(I_16[11]), .out(multiplexer_5_out), .sel(enable_bit));  // open: en
  flip_flop flip_flop_4 (.D(multiplexer_4_out), .Clock(clock), .clear(clear), .Q(Q_16[12]));
  Multiplexer multiplexer_6 (.in0(Q_16[10]), .in1(I_16[10]), .out(multiplexer_6_out), .sel(enable_bit));  // open: en
  flip_flop flip_flop_5 (.D(multiplexer_5_out), .Clock(clock), .clear(clear), .Q(Q_16[11]));
  Multiplexer multiplexer_7 (.in0(Q_16[9]), .in1(I_16[9]), .out(multiplexer_7_out), .sel(enable_bit));  // open: en
  flip_flop flip_flop_6 (.D(multiplexer_6_out), .Clock(clock), .clear(clear), .Q(Q_16[10]));
  Multiplexer multiplexer_8 (.in0(Q_16[8]), .in1(I_16[8]), .out(multiplexer_8_out), .sel(enable_bit));  // open: en
  flip_flop flip_flop_7 (.D(multiplexer_7_out), .Clock(clock), .clear(clear), .Q(Q_16[9]));
  Multiplexer multiplexer_9 (.in0(Q_16[7]), .in1(I_16[7]), .out(multiplexer_9_out), .sel(enable_bit));  // open: en
  flip_flop flip_flop_8 (.D(multiplexer_8_out), .Clock(clock), .clear(clear), .Q(Q_16[8]));
  Multiplexer multiplexer_10 (.in0(Q_16[6]), .in1(I_16[6]), .out(multiplexer_10_out), .sel(enable_bit));  // open: en
  flip_flop flip_flop_9 (.D(multiplexer_9_out), .Clock(clock), .clear(clear), .Q(Q_16[7]));
  Multiplexer multiplexer_11 (.in0(Q_16[5]), .in1(I_16[5]), .out(multiplexer_11_out), .sel(enable_bit));  // open: en
  flip_flop flip_flop_10 (.D(multiplexer_10_out), .Clock(clock), .clear(clear), .Q(Q_16[6]));
  Multiplexer multiplexer_12 (.in0(Q_16[4]), .in1(I_16[4]), .out(multiplexer_12_out), .sel(enable_bit));  // open: en
  flip_flop flip_flop_11 (.D(multiplexer_11_out), .Clock(clock), .clear(clear), .Q(Q_16[5]));
  Multiplexer multiplexer_13 (.in0(Q_16[3]), .in1(I_16[3]), .out(multiplexer_13_out), .sel(enable_bit));  // open: en
  flip_flop flip_flop_12 (.D(multiplexer_12_out), .Clock(clock), .clear(clear), .Q(Q_16[4]));
  Multiplexer multiplexer_14 (.in0(Q_16[2]), .in1(I_16[2]), .out(multiplexer_14_out), .sel(enable_bit));  // open: en
  flip_flop flip_flop_13 (.D(multiplexer_13_out), .Clock(clock), .clear(clear), .Q(Q_16[3]));
  Multiplexer multiplexer_15 (.in0(Q_16[1]), .in1(I_16[1]), .out(multiplexer_15_out), .sel(enable_bit));  // open: en
  flip_flop flip_flop_14 (.D(multiplexer_14_out), .Clock(clock), .clear(clear), .Q(Q_16[2]));
  Multiplexer multiplexer_16 (.in0(Q_16[0]), .in1(I_16[0]), .out(multiplexer_16_out), .sel(enable_bit));  // open: en
  flip_flop flip_flop_15 (.D(multiplexer_15_out), .Clock(clock), .clear(clear), .Q(Q_16[1]));
  flip_flop flip_flop_16 (.D(multiplexer_16_out), .Clock(clock), .clear(clear), .Q(Q_16[0]));
endmodule

module register_memory (
  input  [15:0] data,
  input  write_enable,
  input  [2:0] write_select_reg,
  input  clear,
  input  clock,
  input  [2:0] read_reg1,
  input  [2:0] read_reg2,
  output [15:0] reg1_value,
  output [15:0] reg2_value
);

  wire and_1_out, and_2_out, and_3_out, and_4_out, and_5_out, and_6_out, and_7_out, and_8_out,
       decoder_1_out0, decoder_1_out1, decoder_1_out2, decoder_1_out3, decoder_1_out4, decoder_1_out5,
       decoder_1_out6, decoder_1_out7;
  wire [15:0] R0_q_16, R1_q_16, R2_q_16, R3_q_16, R4_q_16, R5_q_16, R6_q_16, R7_q_16;

  Decoder #(.select(3)) decoder_1 (
    .out0(decoder_1_out0), .out1(decoder_1_out1), .out2(decoder_1_out2), .out3(decoder_1_out3),
    .out4(decoder_1_out4), .out5(decoder_1_out5), .out6(decoder_1_out6), .out7(decoder_1_out7),
    .sel(write_select_reg));  // open: en
  and and_1 (and_1_out, decoder_1_out0, write_enable);
  and and_2 (and_2_out, decoder_1_out1, write_enable);
  and and_3 (and_3_out, decoder_1_out2, write_enable);
  and and_4 (and_4_out, decoder_1_out3, write_enable);
  and and_5 (and_5_out, decoder_1_out4, write_enable);
  and and_6 (and_6_out, decoder_1_out5, write_enable);
  and and_7 (and_7_out, decoder_1_out6, write_enable);
  and and_8 (and_8_out, decoder_1_out7, write_enable);
  _16bit_register R0 (.enable_bit(and_1_out), .clock(clock), .clear(clear), .I_16(data), .Q_16(R0_q_16));
  _16bit_register R1 (.enable_bit(and_2_out), .clock(clock), .clear(clear), .I_16(data), .Q_16(R1_q_16));
  _16bit_register R2 (.enable_bit(and_3_out), .clock(clock), .clear(clear), .I_16(data), .Q_16(R2_q_16));
  _16bit_register R3 (.enable_bit(and_4_out), .clock(clock), .clear(clear), .I_16(data), .Q_16(R3_q_16));
  _16bit_register R4 (.enable_bit(and_5_out), .clock(clock), .clear(clear), .I_16(data), .Q_16(R4_q_16));
  _16bit_register R5 (.enable_bit(and_6_out), .clock(clock), .clear(clear), .I_16(data), .Q_16(R5_q_16));
  _16bit_register R6 (.enable_bit(and_7_out), .clock(clock), .clear(clear), .I_16(data), .Q_16(R6_q_16));
  _16bit_register R7 (.enable_bit(and_8_out), .clock(clock), .clear(clear), .I_16(data), .Q_16(R7_q_16));
  Multiplexer #(.select(3), .width(16)) multiplexer_1 (
    .in0(R0_q_16), .in1(R1_q_16), .in2(R2_q_16), .in3(R3_q_16), .in4(R4_q_16), .in5(R5_q_16), .in6(R6_q_16),
    .in7(R7_q_16), .out(reg1_value), .sel(read_reg1));  // open: en
  Multiplexer #(.select(3), .width(16)) multiplexer_2 (
    .in0(R0_q_16), .in1(R1_q_16), .in2(R2_q_16), .in3(R3_q_16), .in4(R4_q_16), .in5(R5_q_16), .in6(R6_q_16),
    .in7(R7_q_16), .out(reg2_value), .sel(read_reg2));  // open: en
endmodule
